# Fritzing sketch Controlling LED by Potentiometer (saved by Fritzing 0.9.3b)
breadboards: 1

parts:
  LED_RED = LED - 5mm [color="Red (633nm)" package="5 mm [THT]"]
  R1 = Resistor [tolerance=±5% resistance=220 package=THT]
  元件2 = Arduino Mega ADK (Rev3)
  R4 = Potentiometer [package=THT]

nets:
  N1: LED_RED.cathode, 元件2.GND, R4.leg2
  N2: LED_RED.anode, R1.Pin_0
  N3: R1.Pin_1, 元件2.D9_PWM
  N4: 元件2.A0, R4.wiper
  N5: 元件2.5V, R4.leg1

custom parts:
  Arduino Mega ADK (Rev3): The Arduino ADK is a microcontroller board based on the ATmega2560 (datasheet). It has a USB host interface to connect with Android based phones, based on the MAX3421e IC. It has 54 digital input/output pins (of which 14 can be used as PWM outputs), 16 analog inputs, 4 UARTs (hardware serial ports), a 16 MHz crystal oscillator, a USB connection, a power jack, an ICSP header, and a reset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
  Potentiometer: A standard adjustable resistor (potentiometer).
