# Fritzing sketch Lesson 11 Photoresistor (saved by Fritzing 0.8.7b)
breadboards: 1

parts:
  LED2 = LED - 5mm [color="Red (633nm)" package="5 mm [THT]"]
  R5 = Photocell (LDR) [package=THT]
  LED3 = LED - 5mm [color="Red (633nm)" package="5 mm [THT]"]
  LED4 = LED - 5mm [color="Yellow (592nm)" package="5 mm [THT]"]
  LED5 = LED - 5mm [color="Red (633nm)" package="5 mm [THT]"]
  LED6 = LED - 5mm [color="Green (565nm)" package="5 mm [THT]"]
  LED7 = LED - 5mm [color="Yellow (592nm)" package="5 mm [THT]"]
  LED8 = LED - 5mm [color="Green (565nm)" package="5 mm [THT]"]
  LED9 = LED - 5mm [color="Red (633nm)" package="5 mm [THT]"]
  元件2 = Arduino Mega ADK (Rev3)
  R13 = Resistor [tolerance=±5% resistance=220 package=THT]
  R14 = Resistor [tolerance=±5% resistance=220 package=THT]
  R15 = Resistor [tolerance=±5% resistance=220 package=THT]
  R16 = Resistor [tolerance=±5% resistance=220 package=THT]
  R17 = Resistor [tolerance=±5% resistance=220 package=THT]
  R18 = Resistor [tolerance=±5% resistance=220 package=THT]
  R19 = Resistor [tolerance=±5% resistance=220 package=THT]
  R20 = Resistor [tolerance=±5% resistance=220 package=THT]
  R6 = Resistor [tolerance=±5% resistance=10k package=THT]

nets:
  N1: LED2.cathode, LED3.cathode, LED4.cathode, LED5.cathode, LED6.cathode, LED7.cathode, LED8.cathode, LED9.cathode, 元件2.GND, R6.Pin_1
  N2: LED2.anode, R20.Pin_1
  N3: R5.pin_0, 元件2.5V
  N4: R5.pin_1, 元件2.A0, R6.Pin_0
  N5: LED3.anode, R19.Pin_1
  N6: LED4.anode, R17.Pin_1
  N7: LED5.anode, R14.Pin_1
  N8: LED6.anode, R15.Pin_1
  N9: LED7.anode, R18.Pin_1
  N10: LED8.anode, R16.Pin_1
  N11: LED9.anode, R13.Pin_1
  N12: 元件2.D12_PWM, R20.Pin_0
  N13: 元件2.D11_PWM, R19.Pin_0
  N14: 元件2.D10_PWM, R18.Pin_0
  N15: 元件2.D9_PWM, R17.Pin_0
  N16: 元件2.D8_PWM, R16.Pin_0
  N17: 元件2.D5_PWM, R13.Pin_0
  N18: 元件2.D6_PWM, R14.Pin_0
  N19: 元件2.D7_PWM, R15.Pin_0

custom parts:
  Arduino Mega ADK (Rev3): The Arduino ADK is a microcontroller board based on the ATmega2560 (datasheet). It has a USB host interface to connect with Android based phones, based on the MAX3421e IC. It has 54 digital input/output pins (of which 14 can be used as PWM outputs), 16 analog inputs, 4 UARTs (hardware serial ports), a 16 MHz crystal oscillator, a USB connection, a power jack, an ICSP header, and a reset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
