# Fritzing sketch Lesson 13 LCD1602 (saved by Fritzing 0.9.3b)
breadboards: 1

parts:
  元件2 = Arduino Mega ADK (Rev3)
  LCD1 = LCD screen
  R6 = Potentiometer [package=THT]

nets:
  GND: 元件2.GND, LCD1.VSS, LCD1.R/W, LCD1.LED-, R6.leg2
  N1: 元件2.D13_PWM, LCD1.DB7
  N2: 元件2.D12_PWM, LCD1.DB6
  N3: 元件2.D11_PWM, LCD1.DB5
  N4: 元件2.D10_PWM, LCD1.DB4
  N5: 元件2.3V3, LCD1.LED+
  5V: 元件2.5V, LCD1.VDD, R6.leg1
  N6: 元件2.D4_PWM, LCD1.RS
  N7: 元件2.D6_PWM, LCD1.E
  N8: LCD1.V0, R6.wiper

custom parts:
  Arduino Mega ADK (Rev3): The Arduino ADK is a microcontroller board based on the ATmega2560 (datasheet). It has a USB host interface to connect with Android based phones, based on the MAX3421e IC. It has 54 digital input/output pins (of which 14 can be used as PWM outputs), 16 analog inputs, 4 UARTs (hardware serial ports), a 16 MHz crystal oscillator, a USB connection, a power jack, an ICSP header, and a reset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
  LCD screen: A standard character display, usually with 2x16 characters. Comes in many colors.
  Potentiometer: A standard adjustable resistor (potentiometer).
