# Fritzing sketch Lesson 16 Infrared-Receiver (saved by Fritzing 0.9.3b)

parts:
  元件2 = Arduino Mega ADK (Rev3)
  module2 = Ir Receiver-v1.0

nets:
  N1: 元件2.GND, module2._
  N2: 元件2.5V, module2.+
  N3: 元件2.D2_PWM, module2.s

custom parts:
  Arduino Mega ADK (Rev3): The Arduino ADK is a microcontroller board based on the ATmega2560 (datasheet). It has a USB host interface to connect with Android based phones, based on the MAX3421e IC. It has 54 digital input/output pins (of which 14 can be used as PWM outputs), 16 analog inputs, 4 UARTs (hardware serial ports), a 16 MHz crystal oscillator, a USB connection, a power jack, an ICSP header, and a reset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
  Ir Receiver-v1.0: Infrared-Receiver module of SunFounder Sensor Kit
