# Fritzing sketch Lesson 18 Joystick PS2 (saved by Fritzing 0.8.7b)

parts:
  S1 = Joystick PS2 v1.0 [package=THT]
  元件2 = Arduino Mega ADK (Rev3)

nets:
  GND: S1.GND, 元件2.GND
  VCC: S1.VCC, 元件2.5V
  N1: S1.VRX, 元件2.A0
  N2: S1.VRY, 元件2.A1
  N3: S1.SW, 元件2.D8_PWM

custom parts:
  Joystick PS2 v1.0: A joystick is an input device consisting of a stick that pivots on a base and reports its angle or direction to the device it is controlling. Joysticks are often used to control video games and robots. A Joystick PS2 is used here.
  Arduino Mega ADK (Rev3): The Arduino ADK is a microcontroller board based on the ATmega2560 (datasheet). It has a USB host interface to connect with Android based phones, based on the MAX3421e IC. It has 54 digital input/output pins (of which 14 can be used as PWM outputs), 16 analog inputs, 4 UARTs (hardware serial ports), a 16 MHz crystal oscillator, a USB connection, a power jack, an ICSP header, and a reset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
