# Fritzing sketch Lesson 19 7-Segment Display (saved by Fritzing 0.8.7b)
breadboards: 1

parts:
  DI1 = 7-Segment LED Display [package=THT]
  R7 = Resistor [tolerance=±5% resistance=220 package=THT]
  R8 = Resistor [tolerance=±5% resistance=220 package=THT]
  R6 = Resistor [tolerance=±5% resistance=220 package=THT]
  R5 = Resistor [tolerance=±5% resistance=220 package=THT]
  R4 = Resistor [tolerance=±5% resistance=220 package=THT]
  R3 = Resistor [tolerance=±5% resistance=220 package=THT]
  R2 = Resistor [tolerance=±5% resistance=220 package=THT]
  R1 = Resistor [tolerance=±5% resistance=220 package=THT]
  元件2 = Arduino Mega ADK (Rev3)

nets:
  N1: DI1.cathodeE, R6.Pin_1
  N2: DI1.cathodeD, R5.Pin_1
  N3: DI1.commAnode#2, 元件2.GND
  N4: DI1.cathodeC, R8.Pin_0
  N5: DI1.cathodeDP, R7.Pin_0
  N6: DI1.cathodeB, R1.Pin_0
  N7: DI1.cathodeA, R2.Pin_0
  N8: DI1.cathodeF, R3.Pin_1
  N9: DI1.cathodeG, R4.Pin_1
  N10: R7.Pin_1, 元件2.D4_PWM
  N11: R8.Pin_1, 元件2.D5_PWM
  N12: R6.Pin_0, 元件2.D10_PWM
  N13: R5.Pin_0, 元件2.D11_PWM
  N14: R4.Pin_0, 元件2.D9_PWM
  N15: R3.Pin_0, 元件2.D8_PWM
  N16: R2.Pin_1, 元件2.D7_PWM
  N17: R1.Pin_1, 元件2.D6_PWM

custom parts:
  Arduino Mega ADK (Rev3): The Arduino ADK is a microcontroller board based on the ATmega2560 (datasheet). It has a USB host interface to connect with Android based phones, based on the MAX3421e IC. It has 54 digital input/output pins (of which 14 can be used as PWM outputs), 16 analog inputs, 4 UARTs (hardware serial ports), a 16 MHz crystal oscillator, a USB connection, a power jack, an ICSP header, and a reset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
