# Fritzing sketch Stepper Motor driver (saved by Fritzing 0.9.3b)
breadboards: 1

parts:
  module1 = Step Motor
  U2 = Stepper Motor Driver-v1.0 [package="DIP28 [THT]"]
  元件2 = Arduino Mega ADK (Rev3)
  R2 = Potentiometer [package=THT]

nets:
  N1: module1.yellow, U2.OUT3
  N2: module1.orange, U2.OUT4
  N3: module1.red, U2.COM
  N4: module1.pink, U2.OUT2
  N5: module1.blue, U2.OUT1
  N6: U2.IN1, 元件2.D2_PWM
  N7: U2.IN2, 元件2.D4_PWM
  N8: U2.IN3, 元件2.D3_PWM
  N9: U2.IN4, 元件2.D5_PWM
  N10: U2.-, 元件2.GND, R2.leg1
  N11: U2.+, 元件2.5V, R2.leg2
  N12: U2.JD-VCC, U2.VCC
  N13: 元件2.A0, R2.wiper

notes:
  Stepper Motor Driver

custom parts:
  Step Motor: step motor
  Stepper Motor Driver-v1.0: Stepper Motor Driver
  Arduino Mega ADK (Rev3): The Arduino ADK is a microcontroller board based on the ATmega2560 (datasheet). It has a USB host interface to connect with Android based phones, based on the MAX3421e IC. It has 54 digital input/output pins (of which 14 can be used as PWM outputs), 16 analog inputs, 4 UARTs (hardware serial ports), a 16 MHz crystal oscillator, a USB connection, a power jack, an ICSP header, and a reset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
  Potentiometer: A standard adjustable resistor (potentiometer).
