# Fritzing sketch stopwatah (saved by Fritzing 0.9.3b)
breadboards: 1

parts:
  LED2 = 7-SEGMENT-4DIGIT-YOUNGSUN [package=7-segment-4digit-youngsun-longpads]
  元件2 = Arduino Mega ADK (Rev3)
  R1 = Resistor [tolerance=±5% resistance=220 package=THT]
  R7 = Resistor [tolerance=±5% resistance=220 package=THT]
  R6 = Resistor [tolerance=±5% resistance=220 package=THT]
  R8 = Resistor [tolerance=±5% resistance=220 package=THT]
  R5 = Resistor [tolerance=±5% resistance=220 package=THT]
  R4 = Resistor [tolerance=±5% resistance=220 package=THT]
  R3 = Resistor [tolerance=±5% resistance=220 package=THT]
  R2 = Resistor [tolerance=±5% resistance=220 package=THT]

nets:
  N1: LED2.DIG2, R4.Pin_1
  N2: LED2.D, R5.Pin_1
  N3: LED2.COL-A, R7.Pin_0
  N4: LED2.E, R6.Pin_0
  N5: LED2.DIG3, R8.Pin_0
  N6: LED2.DP, 元件2.D10_PWM
  N7: LED2.APOS-A, R1.Pin_0
  N8: LED2.F, 元件2.D11_PWM
  N9: LED2.COL-C, 元件2.D12_PWM
  N10: LED2.C, R2.Pin_1
  N11: LED2.A, R3.Pin_1
  N12: LED2.G, 元件2.D13_PWM
  N13: 元件2.D9_PWM, R7.Pin_1
  N14: 元件2.D8_PWM, R8.Pin_1
  N15: 元件2.D2_PWM, R3.Pin_0
  N16: 元件2.D3_PWM, R1.Pin_1
  N17: 元件2.D4_PWM, R6.Pin_1
  N18: 元件2.D5_PWM, R5.Pin_0
  N19: 元件2.D6_PWM, R4.Pin_0
  N20: 元件2.D7_PWM, R2.Pin_0

custom parts:
  7-SEGMENT-4DIGIT-YOUNGSUN: This is a part for the 4-Digit 7-segment LEDs from Young Sun. Different from the Digikey LEDs, all 16 pins are used. The LONGPADS Variant is used for a test jig, but you may like it because there is more pad to solder to. If you are concerned about routing space, the standard works just fine though.
  Arduino Mega ADK (Rev3): The Arduino ADK is a microcontroller board based on the ATmega2560 (datasheet). It has a USB host interface to connect with Android based phones, based on the MAX3421e IC. It has 54 digital input/output pins (of which 14 can be used as PWM outputs), 16 analog inputs, 4 UARTs (hardware serial ports), a 16 MHz crystal oscillator, a USB connection, a power jack, an ICSP header, and a reset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
