# Fritzing sketch Answer_Machine (saved by Fritzing 0.9.3b)
breadboards: 1

parts:
  LED2 = LED - 5mm [color="Green (565nm)" package="5 mm [THT]"]
  LED3 = LED - 5mm [color="Yellow (595nm)" package="5 mm [THT]"]
  LED4 = LED - 5mm [color="Red (633nm)" package="5 mm [THT]"]
  J1 = Piezo Speaker
  LED1 = smd LED [color="Blue (470nm)" package="0805 [SMD]"]
  LED1_2 = smd LED [color="Red (633nm)" package="1206 [SMD]"]
  元件2 = Arduino Mega ADK (Rev3)
  S5 = Pushbutton [package="[THT]"]
  S6 = Pushbutton [package="[THT]"]
  S7 = Pushbutton [package="[THT]"]
  S8 = Pushbutton [package="[THT]"]
  R3 = Resistor [tolerance=±5% resistance=220 package=THT]
  R4 = Resistor [tolerance=±5% resistance=220 package=THT]
  R5 = Resistor [tolerance=±5% resistance=220 package=THT]
  R6 = Resistor [tolerance=±5% resistance=220 package=THT]

nets:
  N1: LED2.cathode, LED3.cathode, LED4.cathode, J1.pin1, LED1.cathode, LED1_2.cathode, 元件2.GND, S5.Pin_1, S5.Pin_2, S6.Pin_1, S6.Pin_2, S7.Pin_1, S7.Pin_2, S8.Pin_3, S8.Pin_4
  N2: LED2.anode, R5.Pin_1
  N3: LED3.anode, R6.Pin_1
  N4: LED4.anode, R3.Pin_1
  N5: J1.pin2, 元件2.D5_PWM
  N6: LED1.anode, LED1_2.anode, R4.Pin_1
  N7: 元件2.D10_PWM, R6.Pin_0
  N8: 元件2.D9_PWM, S8.Pin_1, S8.Pin_2
  N9: 元件2.D8_PWM, R5.Pin_0
  N10: 元件2.D2_PWM, S7.Pin_3, S7.Pin_4
  N11: 元件2.D3_PWM, S6.Pin_3, S6.Pin_4
  N12: 元件2.D4_PWM, S5.Pin_3, S5.Pin_4
  N13: 元件2.D6_PWM, R3.Pin_0
  N14: 元件2.D7_PWM, R4.Pin_0

custom parts:
  Arduino Mega ADK (Rev3): The Arduino ADK is a microcontroller board based on the ATmega2560 (datasheet). It has a USB host interface to connect with Android based phones, based on the MAX3421e IC. It has 54 digital input/output pins (of which 14 can be used as PWM outputs), 16 analog inputs, 4 UARTs (hardware serial ports), a 16 MHz crystal oscillator, a USB connection, a power jack, an ICSP header, and a reset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
  Pushbutton: A generic pushbutton.
