# Fritzing sketch Lesson 24 Simple Creation-Small Fan (saved by Fritzing 0.9.3b)
circuit board: 8.46667cm x 5.64444cm
breadboards: 1

parts:
  IC1 = L293D [package=THT]
  M1 = DC Motor
  R6 = Resistor [tolerance=±5% resistance=10k package=THT]
  元件2 = Arduino Mega ADK (Rev3)
  S3 = Pushbutton [package="[THT]"]
  C1 = Capacitor [package=cap-pth-small2]

nets:
  N1: IC1.Enable_1, IC1.+Vmotor, IC1.+V, 元件2.5V, S3.Pin_1, S3.Pin_2
  N2: IC1.In_1, 元件2.D10_PWM
  N3: IC1.Out_1_(_Controlled_by_Enable_1_), M1.pin_2
  N4: IC1.0V, R6.Pin_0, 元件2.GND, C1.1
  N5: IC1.Out_2_(_Controlled_by_Enable_1_), M1.pin_1
  N6: IC1.In_2, 元件2.D9_PWM
  N7: R6.Pin_1, 元件2.D2_PWM, S3.Pin_3, S3.Pin_4, C1.2

custom parts:
  Arduino Mega ADK (Rev3): The Arduino ADK is a microcontroller board based on the ATmega2560 (datasheet). It has a USB host interface to connect with Android based phones, based on the MAX3421e IC. It has 54 digital input/output pins (of which 14 can be used as PWM outputs), 16 analog inputs, 4 UARTs (hardware serial ports), a 16 MHz crystal oscillator, a USB connection, a power jack, an ICSP header, and a reset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
  Pushbutton: A generic pushbutton.
  Capacitor: Capacitor Standard 0603 ceramic capacitor, and 0.1 leaded capacitor.
