# Fritzing sketch Simple Creation - Digital Dice (saved by Fritzing 0.9.3b)
breadboards: 1

parts:
  U1 = 74HC595 [package="DIP16 [THT]"]
  DI1 = 7-Segment LED Display [package=THT]
  R8 = Resistor [tolerance=±5% resistance=220 package=THT]
  R6 = Resistor [tolerance=±5% resistance=220 package=THT]
  R1 = Resistor [tolerance=±5% resistance=220 package=THT]
  R4 = Resistor [tolerance=±5% resistance=220 package=THT]
  R2 = Resistor [tolerance=±5% resistance=220 package=THT]
  R7 = Resistor [tolerance=±5% resistance=220 package=THT]
  R5 = Resistor [tolerance=±5% resistance=220 package=THT]
  R3 = Resistor [tolerance=±5% resistance=220 package=THT]
  R9 = Resistor [tolerance=±5% resistance=10k package=THT]
  元件2 = Arduino Mega ADK (Rev3)
  S2 = Pushbutton [package="[THT]"]
  C1 = Capacitor [package=cap-pth-small2]

nets:
  N1: U1.Q1, R3.Pin_0
  N2: U1.Q2, R5.Pin_0
  N3: U1.Q3, R2.Pin_0
  N4: U1.Q5, R8.Pin_1
  N5: U1.Q6, R7.Pin_1
  N6: U1.Q7, R4.Pin_1
  GND: U1.GND, U1.OE, DI1.commAnode#2, R9.Pin_1, 元件2.GND, C1.2
  VCC: U1.MR, U1.VCC, 元件2.5V, S2.Pin_3, S2.Pin_4
  N7: U1.SH_CP, 元件2.D8_PWM
  N8: U1.ST_CP, 元件2.D12_PWM
  N9: U1.DS, 元件2.D11_PWM
  N10: U1.Q0, R6.Pin_1
  N11: DI1.cathodeE, R2.Pin_1
  N12: DI1.cathodeD, R1.Pin_1
  N13: DI1.cathodeC, R8.Pin_0
  N14: DI1.cathodeDP, R6.Pin_0
  N15: DI1.cathodeB, R7.Pin_0
  N16: DI1.cathodeA, R4.Pin_0
  N17: DI1.cathodeF, R5.Pin_1
  N18: DI1.cathodeG, R3.Pin_1
  N19: R9.Pin_0, 元件2.D2_PWM, S2.Pin_1, S2.Pin_2, C1.1

custom parts:
  Arduino Mega ADK (Rev3): The Arduino ADK is a microcontroller board based on the ATmega2560 (datasheet). It has a USB host interface to connect with Android based phones, based on the MAX3421e IC. It has 54 digital input/output pins (of which 14 can be used as PWM outputs), 16 analog inputs, 4 UARTs (hardware serial ports), a 16 MHz crystal oscillator, a USB connection, a power jack, an ICSP header, and a reset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
  Pushbutton: A generic pushbutton.
  Capacitor: Capacitor Standard 0603 ceramic capacitor, and 0.1 leaded capacitor.
