# Fritzing sketch Lesson 6 Doorbell (saved by Fritzing 0.9.3b)
breadboards: 1

parts:
  R1 = Resistor [tolerance=±5% resistance=10k package=THT]
  元件2 = Arduino Mega ADK (Rev3)
  J1 = Piezo Speaker
  S1 = Pushbutton [package="[THT]"]
  C1 = Capacitor [package=cap-pth-small2]

nets:
  N1: R1.Pin_0, 元件2.GND, J1.pin1, C1.1
  N2: R1.Pin_1, 元件2.D2_PWM, S1.Pin_3, S1.Pin_4, C1.2
  N3: 元件2.D8_PWM, J1.pin2
  N4: 元件2.5V, S1.Pin_1, S1.Pin_2

custom parts:
  Arduino Mega ADK (Rev3): The Arduino ADK is a microcontroller board based on the ATmega2560 (datasheet). It has a USB host interface to connect with Android based phones, based on the MAX3421e IC. It has 54 digital input/output pins (of which 14 can be used as PWM outputs), 16 analog inputs, 4 UARTs (hardware serial ports), a 16 MHz crystal oscillator, a USB connection, a power jack, an ICSP header, and a reset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
  Pushbutton: A generic pushbutton.
  Capacitor: Capacitor Standard 0603 ceramic capacitor, and 0.1 leaded capacitor.
