# Fritzing sketch Lesson 8 Relay (saved by Fritzing 0.9.3b)
breadboards: 1

parts:
  Q1 = NPN-Transistor [package="TO92 [THT]"]
  D1 = Rectifier Diode [part_number=1N4001 package="300 mil [THT]"]
  LED1 = LED - 5mm [color="Red (633nm)" package="5 mm [THT]"]
  R3 = Resistor [tolerance=±5% resistance=1k package=THT]
  R2 = Resistor [tolerance=±5% resistance=220 package=THT]
  元件2 = Arduino Mega ADK (Rev3)
  K1 = Relay [part_number=FRS1B-S package=THT]

nets:
  N1: Q1.E, LED1.cathode, 元件2.GND
  N2: Q1.B, R3.Pin_0
  N3: Q1.C, D1.anode, K1.COIL1
  N4: D1.cathode, 元件2.IOREF, 元件2.5V, K1.C1, K1.C2, K1.COIL2
  N5: LED1.anode, R2.Pin_1
  N6: R3.Pin_1, 元件2.D8_PWM
  N7: R2.Pin_0, K1.B

custom parts:
  Arduino Mega ADK (Rev3): The Arduino ADK is a microcontroller board based on the ATmega2560 (datasheet). It has a USB host interface to connect with Android based phones, based on the MAX3421e IC. It has 54 digital input/output pins (of which 14 can be used as PWM outputs), 16 analog inputs, 4 UARTs (hardware serial ports), a 16 MHz crystal oscillator, a USB connection, a power jack, an ICSP header, and a reset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
  Relay: An SPDT relay.
