# Fritzing sketch Lesson 9 RGB LED (saved by Fritzing 0.8.7b)
breadboards: 1

parts:
  LED1 = RGB LED (com. anode, rbg) [package="5 mm [THT]"]
  R2 = Resistor [tolerance=±5% resistance=220 package=THT]
  R3 = Resistor [tolerance=±5% resistance=220 package=THT]
  R1 = Resistor [tolerance=±5% resistance=220 package=THT]
  元件2 = Arduino Mega ADK (Rev3)

nets:
  N1: LED1.red_cathode, R1.Pin_1
  N2: LED1.common_anode, 元件2.GND
  N3: LED1.blue_cathode, R3.Pin_1
  N4: LED1.green_cathode, R2.Pin_1
  N5: R2.Pin_0, 元件2.D9_PWM
  N6: R3.Pin_0, 元件2.D10_PWM
  N7: R1.Pin_0, 元件2.D11_PWM

custom parts:
  Arduino Mega ADK (Rev3): The Arduino ADK is a microcontroller board based on the ATmega2560 (datasheet). It has a USB host interface to connect with Android based phones, based on the MAX3421e IC. It has 54 digital input/output pins (of which 14 can be used as PWM outputs), 16 analog inputs, 4 UARTs (hardware serial ports), a 16 MHz crystal oscillator, a USB connection, a power jack, an ICSP header, and a reset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
