# Fritzing sketch Lesson 12 Servo (saved by Fritzing 0.9.3b)

parts:
  module1 = Servo
  元件2 = SunFounder Uno R3

nets:
  N1: module1.Brown, 元件2.GND
  N2: module1.Red, 元件2.5V
  N3: module1.Orange, 元件2.D9_PWM

custom parts:
  Servo: servo
  SunFounder Uno R3: The Sunfounder Uno is a microcontroller board based on the ATmega328 (datasheet). It has 14 digital input/output pins (of which 6 can be used as PWM outputs), 6 analog inputs, a 16 MHz ceramic resonator, a USB connection, a power jack, an ICSP header, and a reset button. It contains everything needed to support the microcontroller; simply connect it to a computer with a USB cable or power it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
