# Fritzing sketch Lesson 15 Ultrasonic (saved by Fritzing 0.9.3b)
breadboards: 1

parts:
  U1 = HC-SR04 [chip_label=IC package="SIP (Single Inline) [THT]"]
  LCD1 = LCD screen
  R3 = Potentiometer [package=THT]
  元件2 = SunFounder Uno R3

nets:
  VCC: U1.Vcc, LCD1.VDD, R3.leg1, 元件2.5V
  N1: U1.Echo, 元件2.D3_PWM
  GND: U1.GND, LCD1.VSS, LCD1.R/W, LCD1.LED-, R3.leg2, 元件2.GND
  N2: LCD1.V0, R3.wiper
  N3: LCD1.E, 元件2.D6_PWM
  N4: LCD1.LED+, 元件2.3V3

custom parts:
  HC-SR04: HC-SR04 ultrasound distance sensor
  LCD screen: A standard character display, usually with 2x16 characters. Comes in many colors.
  Potentiometer: A standard adjustable resistor (potentiometer).
  SunFounder Uno R3: The Sunfounder Uno is a microcontroller board based on the ATmega328 (datasheet). It has 14 digital input/output pins (of which 6 can be used as PWM outputs), 6 analog inputs, a 16 MHz ceramic resonator, a USB connection, a power jack, an ICSP header, and a reset button. It contains everything needed to support the microcontroller; simply connect it to a computer with a USB cable or power it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
