# Fritzing sketch Lesson 16 Infrared-Receiver (saved by Fritzing 0.9.3b)

parts:
  module2 = Ir Receiver-v1.0
  元件2 = SunFounder Uno R3

nets:
  N1: module2._, 元件2.GND
  N2: module2.+, 元件2.5V
  N3: module2.s, 元件2.D2

custom parts:
  Ir Receiver-v1.0: Infrared-Receiver module of SunFounder Sensor Kit
  SunFounder Uno R3: The Sunfounder Uno is a microcontroller board based on the ATmega328 (datasheet). It has 14 digital input/output pins (of which 6 can be used as PWM outputs), 6 analog inputs, a 16 MHz ceramic resonator, a USB connection, a power jack, an ICSP header, and a reset button. It contains everything needed to support the microcontroller; simply connect it to a computer with a USB cable or power it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
