# Fritzing sketch Lesson 19 7-Segment Display (saved by Fritzing 0.9.3b)
breadboards: 1

parts:
  DI1 = 7-Segment LED Display [package=THT]
  R7 = Resistor [tolerance=±5% resistance=220 package=THT]
  R8 = Resistor [tolerance=±5% resistance=220 package=THT]
  R6 = Resistor [tolerance=±5% resistance=220 package=THT]
  R5 = Resistor [tolerance=±5% resistance=220 package=THT]
  R4 = Resistor [tolerance=±5% resistance=220 package=THT]
  R3 = Resistor [tolerance=±5% resistance=220 package=THT]
  R2 = Resistor [tolerance=±5% resistance=220 package=THT]
  R1 = Resistor [tolerance=±5% resistance=220 package=THT]
  元件2 = SunFounder Uno R3

nets:
  N1: DI1.cathodeE, R6.Pin_1
  N2: DI1.cathodeD, R5.Pin_1
  N3: DI1.commAnode#2, 元件2.GND
  N4: DI1.cathodeC, R8.Pin_0
  N5: DI1.cathodeDP, R7.Pin_0
  N6: DI1.cathodeB, R1.Pin_0
  N7: DI1.cathodeA, R2.Pin_0
  N8: DI1.cathodeF, R3.Pin_1
  N9: DI1.cathodeG, R4.Pin_1
  N10: R8.Pin_1, 元件2.D5_PWM
  N11: R4.Pin_0, 元件2.D9_PWM
  N12: R1.Pin_1, 元件2.D6_PWM

custom parts:
  SunFounder Uno R3: The Sunfounder Uno is a microcontroller board based on the ATmega328 (datasheet). It has 14 digital input/output pins (of which 6 can be used as PWM outputs), 6 analog inputs, a 16 MHz ceramic resonator, a USB connection, a power jack, an ICSP header, and a reset button. It contains everything needed to support the microcontroller; simply connect it to a computer with a USB cable or power it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
