# Fritzing sketch Lesson 21 Stepper Motor (saved by Fritzing 0.9.3b)
breadboards: 1

parts:
  module1 = Step Motor
  U2 = Stepper Motor Driver-v1.0 [package="DIP28 [THT]"]
  R2 = Potentiometer [package=THT]
  元件2 = SunFounder Uno R3

nets:
  N1: module1.yellow, U2.OUT3
  N2: module1.orange, U2.OUT4
  N3: module1.red, U2.COM
  N4: module1.pink, U2.OUT2
  N5: module1.blue, U2.OUT1
  N6: U2.IN1, 元件2.D2
  N7: U2.IN2, 元件2.D4
  N8: U2.IN3, 元件2.D3_PWM
  N9: U2.IN4, 元件2.D5_PWM
  N10: U2.-, R2.leg1, 元件2.GND
  N11: U2.+, R2.leg2
  N12: U2.JD-VCC, U2.VCC
  N13: R2.wiper, 元件2.A0

notes:
  Stepper Motor Driver

custom parts:
  Step Motor: step motor
  Stepper Motor Driver-v1.0: Stepper Motor Driver
  Potentiometer: A standard adjustable resistor (potentiometer).
  SunFounder Uno R3: The Sunfounder Uno is a microcontroller board based on the ATmega328 (datasheet). It has 14 digital input/output pins (of which 6 can be used as PWM outputs), 6 analog inputs, a 16 MHz ceramic resonator, a USB connection, a power jack, an ICSP header, and a reset button. It contains everything needed to support the microcontroller; simply connect it to a computer with a USB cable or power it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
