# Fritzing sketch Lesson 23 Simple Creation-Answer Machine (saved by Fritzing 0.9.3b)
breadboards: 1

parts:
  LED2 = LED - 5mm [color="Green (565nm)" package="5 mm [THT]"]
  LED3 = LED - 5mm [color="Yellow (595nm)" package="5 mm [THT]"]
  LED4 = LED - 5mm [color="Red (633nm)" package="5 mm [THT]"]
  J1 = Piezo Speaker
  LED1 = smd LED [color="Blue (470nm)" package="0805 [SMD]"]
  LED1_2 = smd LED [color="Red (633nm)" package="1206 [SMD]"]
  S5 = Pushbutton [package="[THT]"]
  S6 = Pushbutton [package="[THT]"]
  S7 = Pushbutton [package="[THT]"]
  S8 = Pushbutton [package="[THT]"]
  R3 = Resistor [tolerance=±5% resistance=220 package=THT]
  R4 = Resistor [tolerance=±5% resistance=220 package=THT]
  R5 = Resistor [tolerance=±5% resistance=220 package=THT]
  R6 = Resistor [tolerance=±5% resistance=220 package=THT]
  元件2 = SunFounder Uno R3

nets:
  N1: LED2.cathode, LED3.cathode, LED4.cathode, J1.pin1, LED1.cathode, LED1_2.cathode, S5.Pin_1, S5.Pin_2, S6.Pin_1, S6.Pin_2, S7.Pin_1, S7.Pin_2, S8.Pin_3, S8.Pin_4, 元件2.GND
  N2: LED2.anode, R5.Pin_1
  N3: LED3.anode, R6.Pin_1
  N4: LED4.anode, R3.Pin_1
  N5: J1.pin2, 元件2.D5_PWM
  N6: LED1.anode, LED1_2.anode, R4.Pin_1
  N7: S5.Pin_3, S5.Pin_4
  N8: S6.Pin_3, S6.Pin_4, 元件2.D3_PWM
  N9: S7.Pin_3, S7.Pin_4
  N10: S8.Pin_1, S8.Pin_2, 元件2.D9_PWM
  N11: R3.Pin_0, 元件2.D6_PWM

custom parts:
  Pushbutton: A generic pushbutton.
  SunFounder Uno R3: The Sunfounder Uno is a microcontroller board based on the ATmega328 (datasheet). It has 14 digital input/output pins (of which 6 can be used as PWM outputs), 6 analog inputs, a 16 MHz ceramic resonator, a USB connection, a power jack, an ICSP header, and a reset button. It contains everything needed to support the microcontroller; simply connect it to a computer with a USB cable or power it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
