# Fritzing sketch Lesson 6 Doorbell (saved by Fritzing 0.9.3b)
breadboards: 1

parts:
  R1 = Resistor [tolerance=±5% resistance=10k package=THT]
  J1 = Piezo Speaker
  S1 = Pushbutton [package="[THT]"]
  C1 = Capacitor [package=cap-pth-small2]
  元件2 = SunFounder Uno R3

nets:
  N1: R1.Pin_0, J1.pin1, C1.1, 元件2.GND
  N2: R1.Pin_1, S1.Pin_3, S1.Pin_4, C1.2
  N3: S1.Pin_1, S1.Pin_2, 元件2.5V

custom parts:
  Pushbutton: A generic pushbutton.
  Capacitor: Capacitor Standard 0603 ceramic capacitor, and 0.1 leaded capacitor.
  SunFounder Uno R3: The Sunfounder Uno is a microcontroller board based on the ATmega328 (datasheet). It has 14 digital input/output pins (of which 6 can be used as PWM outputs), 6 analog inputs, a 16 MHz ceramic resonator, a USB connection, a power jack, an ICSP header, and a reset button. It contains everything needed to support the microcontroller; simply connect it to a computer with a USB cable or power it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
